# Fritzing sketch 45_RadarScanning (saved by Fritzing 0.9.2b)
breadboards: 1

parts:
  AdeeptLesson15 = Arduino Uno (Rev3)
  Part1 = Adeept Ultrasonic Distance Sensor Module [part_number="Adeept  Ultrasonic Distance Sensor Module"]
  J1 = Basic Servo

nets:
  N1: AdeeptLesson15.D2, Part1.Trig
  N2: AdeeptLesson15.D3_PWM, Part1.Echo
  N3: AdeeptLesson15.D6_PWM, J1.pulse
  5V: AdeeptLesson15.5V, Part1.+, J1.vcc
  GND: AdeeptLesson15.GND, Part1.-, J1.gnd
