# Fritzing sketch 34_led_Processing (saved by Fritzing 0.9.2b)
breadboards: 1

parts:
  R1 = Resistor [tolerance=±5% resistance=220 package=THT]
  LED1 = LED - 5mm [color="Red (633nm)" package="5 mm [THT]"]
  LED2 = LED - 5mm [color="Green (565nm)" package="5 mm [THT]"]
  R2 = Resistor [tolerance=±5% resistance=220 package=THT]
  LED3 = LED - 5mm [color="Blue (430nm)" package="5 mm [THT]"]
  R3 = Resistor [tolerance=±5% resistance=220 package=THT]
  LED4 = LED - 5mm [color="Yellow (595nm)" package="5 mm [THT]"]
  R4 = Resistor [tolerance=±5% resistance=220 package=THT]
  Part1 = Arduino Mega 2560 (Rev3)

nets:
  N1: R1.Pin_0, R2.Pin_1, R3.Pin_1, R4.Pin_1, Part1.GND
  N2: R1.Pin_1, LED1.cathode
  N3: LED1.anode, Part1.D8_PWM
  N4: LED2.cathode, R2.Pin_0
  N5: LED2.anode, Part1.D9_PWM
  N6: LED3.cathode, R3.Pin_0
  N7: LED3.anode, Part1.D10_PWM
  N8: LED4.cathode, R4.Pin_0
  N9: LED4.anode, Part1.D11_PWM
