# Fritzing sketch 35_Button_Processing (saved by Fritzing 0.9.2b)
breadboards: 1

parts:
  S2 = Pushbutton [package="[THT]"]
  S3 = Pushbutton [package="[THT]"]
  S4 = Pushbutton [package="[THT]"]
  S1 = Pushbutton [package="[THT]"]
  Part1 = Arduino Mega 2560 (Rev3)

nets:
  N1: S2.Pin_1, S2.Pin_2, S3.Pin_3, S3.Pin_4, S4.Pin_3, S4.Pin_4, S1.Pin_1, S1.Pin_2, Part1.GND
  N2: S2.Pin_3, S2.Pin_4, Part1.D9_PWM
  N3: S3.Pin_1, S3.Pin_2, Part1.D10_PWM
  N4: S4.Pin_1, S4.Pin_2, Part1.D11_PWM
  N5: S1.Pin_3, S1.Pin_4, Part1.D8_PWM
