# Fritzing sketch ActiveBuzzerModule_Processing (saved by Fritzing 0.9.2b)
breadboards: 1

parts:
  R1 = Resistor [tolerance=±5% resistance=1k package=THT]
  J1 = Piezo Speaker
  8050 = NPN-Transistor [package="TO92 [THT]"]
  Part1 = Arduino Mega 2560 (Rev3)

nets:
  N1: R1.Pin_0, 8050.B
  N2: R1.Pin_1, Part1.D8_PWM
  N3: J1.pin1, 8050.C
  N4: J1.pin2, Part1.5V
  N5: 8050.E, Part1.GND
