# Fritzing sketch 39_RGB_Processing (saved by Fritzing 0.9.2b)
breadboards: 1

parts:
  R1 = Resistor [tolerance=±5% resistance=220 package=THT]
  R2 = Resistor [tolerance=±5% resistance=220 package=THT]
  R3 = Resistor [tolerance=±5% resistance=220 package=THT]
  LED1 = RGB LED (com. cathode, rgb) [package="5 mm [THT]"]
  Part1 = Arduino Mega 2560 (Rev3)

nets:
  N1: R1.Pin_0, LED1.red_anode
  N2: R1.Pin_1, Part1.D11_PWM
  N3: R2.Pin_0, LED1.green_anode
  N4: R2.Pin_1, Part1.D10_PWM
  N5: R3.Pin_0, LED1.blue_anode
  N6: R3.Pin_1, Part1.D9_PWM
  N7: LED1.common_cathode, Part1.5V
