# Fritzing sketch 40_DS18B20Module_Processing (saved by Fritzing 0.9.2b)
breadboards: 1

parts:
  R5 = Temperature Sensor (Thermistor) [thermistor_type=NTC package=THT]
  R6 = Resistor [tolerance=±5% resistance=10k package=THT]
  Part1 = Arduino Mega 2560 (Rev3)

nets:
  N1: R5.pin_0, R6.Pin_0, Part1.A0
  N2: R5.pin_1, Part1.5V
  N3: R6.Pin_1, Part1.GND
