# Fritzing sketch 42_Move a cat (saved by Fritzing 0.9.2b)
breadboards: 1

parts:
  元件2 = Adeept Ultrasonic Distance Sensor Module [part_number="Adeept  Ultrasonic Distance Sensor Module"]
  Part1 = Arduino Mega 2560 (Rev3)

nets:
  N1: 元件2.-, Part1.GND
  N2: 元件2.+, Part1.5V
  N3: 元件2.Trig, Part1.D7_PWM
  N4: 元件2.Echo, Part1.D5_PWM
