# Fritzing sketch 43_Controlling the 3D model by PS2 Joystick (saved by Fritzing 0.9.2b)

parts:
  元件2 = Adeept Joystick Module [part_number="Adeept Joystick Module"]
  Part1 = Arduino Mega 2560 (Rev3)

nets:
  N1: 元件2.z, Part1.D9_PWM
  N2: 元件2.x, Part1.A0
  N3: 元件2.y, Part1.A1
  N4: 元件2.+, Part1.5V
  N5: 元件2.-, Part1.GND
