# Fritzing sketch 46_The Brick Games (saved by Fritzing 0.9.2b)
breadboards: 1

parts:
  S1 = Pushbutton [package="[THT]"]
  S2 = Pushbutton [package="[THT]"]
  Part1 = Arduino Mega 2560 (Rev3)

nets:
  N1: S1.Pin_1, S1.Pin_2, Part1.D8_PWM
  N2: S1.Pin_3, S1.Pin_4, S2.Pin_1, S2.Pin_2, Part1.GND
  N3: S2.Pin_3, S2.Pin_4, Part1.D7_PWM
