# Fritzing sketch 47_Star Wars (saved by Fritzing 0.9.2b)
breadboards: 1

parts:
  S1 = Pushbutton [package="[THT]"]
  Part1 = Adeept Joystick Module [part_number="Adeept Joystick Module"]
  Part2 = Arduino Mega 2560 (Rev3)

nets:
  N1: S1.Pin_1, S1.Pin_2, Part2.D9_PWM
  N2: S1.Pin_3, S1.Pin_4, Part1.-, Part2.GND
  N3: Part1.x, Part2.A0
  N4: Part1.y, Part2.A1
  N5: Part1.+, Part2.5V
